// Digital circuit Execute.dig as structural Verilog
module Execute (
  input  [7:0] REG_IN,
  input  [2:0] NUMOP,
  input  [4:0] INS,
  input  [7:0] OP_1,
  input  CLK,
  output MEM_IN,
  output MEM_OUT,
  output [2:0] COUNT,
  output [2:0] DREG,
  output [7:0] VALUE,
  output [2:0] SREG,
  output [2:0] RREG,
  output HLT,
  output [7:0] JMP,
  output JMP_COND,
  output [7:0] Flag
);

  wire add_1_c_o, add_2_c_o, and_2_out, and_3_out, and_4_out, and_5_out, and_7_out, and_10_out,
       comparator_1_lt, comparator_2_gt, comparator_3_eq, comparator_4_eq, comparator_5_eq, comparator_6_eq,
       COND_R, COUNT_NZ, COUNT_ONE, COUNT_Z, JZN_R, LD_COND, not_1_out, not_2_out, not_4_out, not_5_out,
       not_6_out, not_7_out, not_8_out, not_9_out, not_10_out, not_11_out, not_12_out, NUMOP_NZ, NUMOP_Z,
       or_2_out, or_3_out, Overflow, sub_1_c_o, sub_2_c_o, ZERO;
  wire [2:0] DEC_REG, DEST, INC_REG, LDA_REG, notconnected_1_out, notconnected_2_out, notconnected_3_out,
       notconnected_4_out, notconnected_5_out, notconnected_6_out, notconnected_7_out, notconnected_8_out,
       notconnected_9_out, notconnected_10_out, notconnected_11_out, notconnected_12_out,
       notconnected_13_out, notconnected_14_out, notconnected_15_out, notconnected_16_out,
       notconnected_17_out, notconnected_18_out, notconnected_19_out, notconnected_20_out,
       notconnected_21_out, notconnected_22_out, notconnected_23_out, notconnected_24_out,
       notconnected_25_out, notconnected_26_out, notconnected_27_out, notconnected_28_out,
       notconnected_29_out, notconnected_30_out, notconnected_31_out, notconnected_32_out,
       notconnected_33_out, notconnected_34_out, notconnected_35_out, notconnected_36_out,
       notconnected_37_out, notconnected_38_out, notconnected_39_out, notconnected_40_out,
       notconnected_41_out, notconnected_42_out, notconnected_43_out, notconnected_44_out,
       notconnected_45_out, notconnected_46_out, notconnected_47_out, notconnected_48_out,
       notconnected_49_out, notconnected_50_out, notconnected_51_out, notconnected_52_out,
       notconnected_53_out, notconnected_54_out, notconnected_55_out, notconnected_56_out,
       notconnected_57_out, notconnected_58_out, notconnected_59_out, SRC, STA_REG;
  wire [4:0] IR;
  wire [7:0] ADD_A, ADD_B, ADD_R, DEC_IN, DEC_OUT, demultiplexer_1_out_1, demultiplexer_1_out_13,
       demultiplexer_1_out_14, INC_IN, INC_OUT, JMP_t, JZE, JZN, LDA_OUT, multiplexer_6_out,
       multiplexer_8_out, multiplexer_10_out, notconnected_60_out, notconnected_61_out, notconnected_62_out,
       notconnected_63_out, notconnected_64_out, notconnected_65_out, notconnected_66_out,
       notconnected_67_out, notconnected_68_out, notconnected_69_out, notconnected_70_out,
       notconnected_71_out, notconnected_72_out, notconnected_73_out, notconnected_74_out,
       notconnected_75_out, notconnected_76_out, notconnected_77_out, notconnected_78_out,
       notconnected_79_out, notconnected_80_out, notconnected_81_out, notconnected_82_out, STA_OUT, SUB_A,
       SUB_B, SUB_R;
  wire [7:3] demultiplexer_1_out_2, demultiplexer_1_out_5, demultiplexer_1_out_6, demultiplexer_1_out_12,
       demultiplexer_1_out_15;

  Multiplexer #(.Selector_Bits(5), .Bits(3)) multiplexer_1 (
    .sel(IR), .in_0(notconnected_1_out), .in_1(3'b100), .in_2(DEST), .in_3(notconnected_2_out),
    .in_4(3'b100), .in_5(INC_REG), .in_6(DEC_REG), .in_7(3'b100), .in_8(3'b111), .in_9(3'b111),
    .in_10(3'b111), .in_11(notconnected_3_out), .in_12(3'b100), .in_13(3'b111), .in_14(3'b100),
    .in_15(3'b111), .in_16(notconnected_4_out), .in_17(notconnected_5_out), .in_18(notconnected_6_out),
    .in_19(notconnected_7_out), .in_20(notconnected_8_out), .in_21(notconnected_9_out),
    .in_22(notconnected_10_out), .in_23(notconnected_11_out), .in_24(notconnected_12_out),
    .in_25(notconnected_13_out), .in_26(notconnected_14_out), .in_27(notconnected_15_out),
    .in_28(notconnected_16_out), .in_29(notconnected_17_out), .in_30(notconnected_18_out),
    .in_31(notconnected_19_out), .out(DREG));
  // NotConnected on notconnected_1_out
  // NotConnected on notconnected_2_out
  // NotConnected on notconnected_3_out
  // NotConnected on notconnected_4_out
  // NotConnected on notconnected_5_out
  // NotConnected on notconnected_6_out
  // NotConnected on notconnected_7_out
  // NotConnected on notconnected_8_out
  // NotConnected on notconnected_9_out
  // NotConnected on notconnected_10_out
  // NotConnected on notconnected_11_out
  // NotConnected on notconnected_12_out
  // NotConnected on notconnected_13_out
  // NotConnected on notconnected_14_out
  // NotConnected on notconnected_15_out
  // NotConnected on notconnected_16_out
  // NotConnected on notconnected_17_out
  // NotConnected on notconnected_18_out
  // NotConnected on notconnected_19_out
  or or_1 (NUMOP_NZ, NUMOP[0], NUMOP[1], NUMOP[2]);
  nor nor_1 (NUMOP_Z, NUMOP[0], NUMOP[1], NUMOP[2]);
  or or_2 (or_2_out, LD_COND, NUMOP_Z);
  Register #(.Bits(5)) u_IR (.D(INS), .C(CLK), .en(or_2_out), .Q(IR));
  Multiplexer #(.Selector_Bits(5), .Bits(3)) multiplexer_2 (
    .sel(IR), .in_0(notconnected_20_out), .in_1(3'b111), .in_2(3'b111), .in_3(notconnected_21_out),
    .in_4(3'b100), .in_5(INC_REG), .in_6(DEC_REG), .in_7(3'b100), .in_8(3'b111), .in_9(3'b000),
    .in_10(3'b000), .in_11(notconnected_22_out), .in_12(LDA_REG), .in_13(notconnected_23_out),
    .in_14(notconnected_24_out), .in_15(STA_REG), .in_16(notconnected_25_out), .in_17(notconnected_26_out),
    .in_18(notconnected_27_out), .in_19(notconnected_28_out), .in_20(notconnected_29_out),
    .in_21(notconnected_30_out), .in_22(notconnected_31_out), .in_23(notconnected_32_out),
    .in_24(notconnected_33_out), .in_25(notconnected_34_out), .in_26(notconnected_35_out),
    .in_27(notconnected_36_out), .in_28(notconnected_37_out), .in_29(notconnected_38_out),
    .in_30(notconnected_39_out), .in_31(notconnected_40_out), .out(RREG));
  // NotConnected on notconnected_20_out
  // NotConnected on notconnected_21_out
  // NotConnected on notconnected_22_out
  // NotConnected on notconnected_23_out
  // NotConnected on notconnected_24_out
  // NotConnected on notconnected_25_out
  // NotConnected on notconnected_26_out
  // NotConnected on notconnected_27_out
  // NotConnected on notconnected_28_out
  // NotConnected on notconnected_29_out
  // NotConnected on notconnected_30_out
  // NotConnected on notconnected_31_out
  // NotConnected on notconnected_32_out
  // NotConnected on notconnected_33_out
  // NotConnected on notconnected_34_out
  // NotConnected on notconnected_35_out
  // NotConnected on notconnected_36_out
  // NotConnected on notconnected_37_out
  // NotConnected on notconnected_38_out
  // NotConnected on notconnected_39_out
  // NotConnected on notconnected_40_out
  or or_3 (or_3_out, COUNT_NZ, NUMOP_NZ);
  and and_1 (LD_COND, NUMOP_NZ, COUNT_Z);
  Multiplexer #(.Selector_Bits(5), .Bits(3)) multiplexer_3 (
    .sel(IR), .in_0(notconnected_41_out), .in_1(3'b111), .in_2(SRC), .in_3(3'b111),
    .in_4(notconnected_42_out), .in_5(3'b111), .in_6(3'b111), .in_7(3'b111), .in_8(3'b111), .in_9(3'b111),
    .in_10(3'b111), .in_11(notconnected_43_out), .in_12(3'b111), .in_13(3'b111), .in_14(3'b111),
    .in_15(3'b111), .in_16(notconnected_44_out), .in_17(notconnected_45_out), .in_18(notconnected_46_out),
    .in_19(notconnected_47_out), .in_20(notconnected_48_out), .in_21(notconnected_49_out),
    .in_22(notconnected_50_out), .in_23(notconnected_51_out), .in_24(notconnected_52_out),
    .in_25(notconnected_53_out), .in_26(notconnected_54_out), .in_27(notconnected_55_out),
    .in_28(notconnected_56_out), .in_29(notconnected_57_out), .in_30(notconnected_58_out),
    .in_31(notconnected_59_out), .out(SREG));
  // NotConnected on notconnected_41_out
  // NotConnected on notconnected_42_out
  // NotConnected on notconnected_43_out
  // NotConnected on notconnected_44_out
  // NotConnected on notconnected_45_out
  // NotConnected on notconnected_46_out
  // NotConnected on notconnected_47_out
  // NotConnected on notconnected_48_out
  // NotConnected on notconnected_49_out
  // NotConnected on notconnected_50_out
  // NotConnected on notconnected_51_out
  // NotConnected on notconnected_52_out
  // NotConnected on notconnected_53_out
  // NotConnected on notconnected_54_out
  // NotConnected on notconnected_55_out
  // NotConnected on notconnected_56_out
  // NotConnected on notconnected_57_out
  // NotConnected on notconnected_58_out
  // NotConnected on notconnected_59_out
  CounterPreset #(.Bits(3)) counterpreset_1 (
    .en(or_3_out), .C(CLK), .dir(1'b1), .in(NUMOP), .ld(LD_COND), .clr(1'b0), .out(COUNT));  // open: ovf
  nor nor_2 (COUNT_Z, COUNT[0], COUNT[1], COUNT[2]);
  or or_4 (COUNT_NZ, COUNT[0], COUNT[1], COUNT[2]);
  not not_1 (not_1_out, IR[3]);
  not not_2 (not_2_out, IR[4]);
  and and_2 (and_2_out, COUNT_NZ, COND_R);
  and and_3 (and_3_out, IR[2], not_1_out, not_2_out);
  Comparator #(.Bits(5)) comparator_1 (.a(IR), .b(5'b01011), .lt(comparator_1_lt));  // open: gt, eq
  Comparator #(.Bits(5)) comparator_2 (.a(IR), .b(5'b00111), .gt(comparator_2_gt));  // open: eq, lt
  Multiplexer #(.Selector_Bits(2), .Bits(8)) multiplexer_4 (
    .sel(IR[1:0]), .in_0(JMP_t), .in_1(JZE), .in_2(JZN), .in_3(notconnected_60_out), .out(JMP));
  // NotConnected on notconnected_60_out
  and and_4 (and_4_out, and_2_out, Flag[1]);
  and and_5 (and_5_out, and_2_out, JZN_R);
  Register u_Overflow (.D(Overflow), .C(CLK), .en(and_3_out), .Q(Flag[0]));
  Register ZeroResult (.D(ZERO), .C(CLK), .en(and_3_out), .Q(Flag[1]));
  and and_6 (COND_R, comparator_1_lt, comparator_2_gt);
  Multiplexer #(.Selector_Bits(2)) multiplexer_5 (
    .sel(IR[1:0]), .in_0(and_2_out), .in_1(and_4_out), .in_2(and_5_out), .in_3(1'b0), .out(JMP_COND));
  not not_3 (JZN_R, Flag[1]);
  not not_4 (not_4_out, IR[0]);
  not not_5 (not_5_out, IR[3]);
  not not_6 (not_6_out, IR[4]);
  Multiplexer #(.Bits(8)) multiplexer_6 (.sel(and_7_out), .in_0({8{1'b1}}), .in_1(DEC_IN), .out(multiplexer_6_out));
  Comparator #(.Bits(8)) comparator_3 (.a(SUB_R), .b({8{1'b0}}), .eq(comparator_3_eq));  // open: gt, lt
  Comparator #(.Bits(8)) comparator_4 (.a(DEC_OUT), .b({8{1'b0}}), .eq(comparator_4_eq));  // open: gt, lt
  and and_7 (and_7_out, not_4_out, IR[1], IR[2], not_5_out, not_6_out);
  Sub #(.Bits(8)) sub_1 (.a(SUB_A), .b(SUB_B), .c_i(1'b0), .s(SUB_R), .c_o(sub_1_c_o));
  Sub #(.Bits(8)) sub_2 (.a(multiplexer_6_out), .b(8'h1), .c_i(1'b0), .s(DEC_OUT), .c_o(sub_2_c_o));
  Add #(.Bits(8)) add_1 (.a(INC_IN), .b(8'h1), .c_i(1'b0), .s(INC_OUT), .c_o(add_1_c_o));
  Add #(.Bits(8)) add_2 (.a(ADD_A), .b(ADD_B), .c_i(1'b0), .s(ADD_R), .c_o(add_2_c_o));
  Multiplexer #(.Selector_Bits(2)) multiplexer_7 (
    .sel(IR[1:0]), .in_0(comparator_6_eq), .in_1(comparator_5_eq), .in_2(comparator_4_eq),
    .in_3(comparator_3_eq), .out(ZERO));
  Comparator #(.Bits(8)) comparator_5 (.a(INC_OUT), .b({8{1'b0}}), .eq(comparator_5_eq));  // open: gt, lt
  Comparator #(.Bits(8)) comparator_6 (.a(ADD_R), .b({8{1'b0}}), .eq(comparator_6_eq));  // open: gt, lt
  or or_5 (Overflow, sub_1_c_o, sub_2_c_o, add_1_c_o, add_2_c_o);
  not not_7 (not_7_out, COUNT[1]);
  not not_8 (not_8_out, COUNT[2]);
  and and_8 (COUNT_ONE, COUNT[0], not_7_out, not_8_out);
  Multiplexer #(.Bits(8)) multiplexer_8 (.sel(COUNT_ONE), .in_0({8{1'b0}}), .in_1(OP_1), .out(multiplexer_8_out));
  Demultiplexer #(.Selector_Bits(5), .Bits(8)) demultiplexer_1 (
    .sel(IR), .in(multiplexer_8_out), .out_1(demultiplexer_1_out_1),
    .out_2({demultiplexer_1_out_2[7], SRC, demultiplexer_1_out_2[3], DEST}), .out_4(ADD_B),
    .out_5({demultiplexer_1_out_5, INC_REG}), .out_6({demultiplexer_1_out_6, DEC_REG}), .out_7(SUB_B),
    .out_8(JMP_t), .out_9(JZE), .out_10(JZN), .out_12({demultiplexer_1_out_12, LDA_REG}),
    .out_13(demultiplexer_1_out_13), .out_14(demultiplexer_1_out_14),
    .out_15({demultiplexer_1_out_15, STA_REG}));  // open: out_0, out_3, out_11, out_16, out_17, out_18, out_19, out_20, out_21, out_22, out_23, out_24, out_25, out_26, out_27, out_28, out_29, out_30, out_31
  not not_9 (not_9_out, IR[2]);
  not not_10 (not_10_out, IR[4]);
  and and_9 (HLT, IR[0], IR[1], not_9_out, IR[3], not_10_out);
  not not_11 (not_11_out, IR[4]);
  Multiplexer #(.Selector_Bits(5), .Bits(8)) multiplexer_9 (
    .sel(IR), .in_0(notconnected_61_out), .in_1(demultiplexer_1_out_1), .in_2({8{1'b0}}),
    .in_3(notconnected_62_out), .in_4(ADD_R), .in_5(INC_OUT), .in_6(DEC_OUT), .in_7(SUB_R),
    .in_8(notconnected_63_out), .in_9(notconnected_64_out), .in_10(notconnected_65_out),
    .in_11(notconnected_66_out), .in_12(LDA_OUT), .in_13(demultiplexer_1_out_13),
    .in_14(demultiplexer_1_out_14), .in_15(STA_OUT), .in_16(notconnected_67_out),
    .in_17(notconnected_68_out), .in_18(notconnected_69_out), .in_19(notconnected_70_out),
    .in_20(notconnected_71_out), .in_21(notconnected_72_out), .in_22(notconnected_73_out),
    .in_23(notconnected_74_out), .in_24(notconnected_75_out), .in_25(notconnected_76_out),
    .in_26(notconnected_77_out), .in_27(notconnected_78_out), .in_28(notconnected_79_out),
    .in_29(notconnected_80_out), .in_30(notconnected_81_out), .in_31(notconnected_82_out), .out(VALUE));
  // NotConnected on notconnected_61_out
  // NotConnected on notconnected_62_out
  // NotConnected on notconnected_63_out
  // NotConnected on notconnected_64_out
  // NotConnected on notconnected_65_out
  // NotConnected on notconnected_66_out
  // NotConnected on notconnected_67_out
  // NotConnected on notconnected_68_out
  // NotConnected on notconnected_69_out
  // NotConnected on notconnected_70_out
  // NotConnected on notconnected_71_out
  // NotConnected on notconnected_72_out
  // NotConnected on notconnected_73_out
  // NotConnected on notconnected_74_out
  // NotConnected on notconnected_75_out
  // NotConnected on notconnected_76_out
  // NotConnected on notconnected_77_out
  // NotConnected on notconnected_78_out
  // NotConnected on notconnected_79_out
  // NotConnected on notconnected_80_out
  // NotConnected on notconnected_81_out
  // NotConnected on notconnected_82_out
  and and_10 (and_10_out, IR[2], IR[3], not_11_out);
  not not_12 (not_12_out, IR[0]);
  and and_11 (MEM_IN, IR[0], and_10_out);
  and and_12 (MEM_OUT, not_12_out, and_10_out);
  Multiplexer #(.Bits(8)) multiplexer_10 (.sel(COUNT_ONE), .in_0({8{1'b0}}), .in_1(REG_IN), .out(multiplexer_10_out));
  Demultiplexer #(.Selector_Bits(5), .Bits(8)) demultiplexer_2 (
    .sel(IR), .in(multiplexer_10_out), .out_4(ADD_A), .out_5(INC_IN), .out_6(DEC_IN), .out_7(SUB_A),
    .out_12(LDA_OUT), .out_15(STA_OUT));  // open: out_0, out_1, out_2, out_3, out_8, out_9, out_10, out_11, out_13, out_14, out_16, out_17, out_18, out_19, out_20, out_21, out_22, out_23, out_24, out_25, out_26, out_27, out_28, out_29, out_30, out_31

  assign Flag[7:2] = {6{1'b0}};

  // Other names for the same wires on the sheet: JZE_R = Flag[1]

  // Notes on the sheet:
  //   Counter and input operations
  //   Register outputs
  //   Jump Condition calculation
  //   Check for jump instruction
  //   Instruction List:
  //   00. NOP
  //   01. MVA <number>
  //   02. MOV <register> <register>
  //   03. --
  //   04. ADD <number>
  //   05. INC <register>
  //   06. DEC <register>
  //   07. SUB <number>
  //   08. JMP <address | label>
  //   09. JZE <address | label>
  //   10. JZN <address | label>
  //   11. HLT
  //   12. LDA <register>
  //   13. STR <address> <- internal use only
  //   14. LOD <address> <- internal use only
  //   15. STA <register>
  //   Operand and register A calculations
endmodule
