// Digital circuit Fetch.dig as structural Verilog
module Fetch (
  input  CLK,
  input  [7:0] JMP,
  input  JMP_COND,
  output [7:0] Addr
);

  CounterPreset #(.Bits(8)) PC (
    .en(1'b1), .C(CLK), .dir(1'b0), .in(JMP), .ld(JMP_COND), .clr(1'b0), .out(Addr));  // open: ovf
endmodule
