// Digital circuit LedDriver.dig as structural Verilog
module LedDriver (
  input  [7:0] A,
  input  [7:0] B,
  input  [7:0] C,
  input  [7:0] D,
  input  E,
  output [7:0] O_A,
  output [7:0] O_B,
  output [7:0] O_C,
  output [7:0] O_D
);

  Register #(.Bits(8)) register_1 (.D(A), .C(E), .en(1'b1), .Q(O_A));
  Register #(.Bits(8)) register_2 (.D(B), .C(E), .en(1'b1), .Q(O_B));
  Register #(.Bits(8)) register_3 (.D(C), .C(E), .en(1'b1), .Q(O_C));
  Register #(.Bits(8)) register_4 (.D(D), .C(E), .en(1'b1), .Q(O_D));
endmodule
