// Digital circuit RegFile.dig as structural Verilog
module RegFile (
  input  [2:0] COUNT,
  input  [2:0] DREG,
  input  [7:0] VALUE,
  input  [2:0] SREG,
  input  [2:0] RREG,
  input  CLK,
  output [7:0] READ_REG,
  output [7:0] REGACC,
  output [7:0] REGA,
  output [7:0] REGB,
  output [7:0] REGC,
  output [7:0] REGD,
  output [7:0] REGE
);

  wire CNT, decoder_1_out_0, decoder_1_out_1, decoder_1_out_2, decoder_1_out_3, decoder_1_out_4,
       decoder_1_out_5, decoder_2_out_0, decoder_2_out_1, decoder_2_out_2, decoder_2_out_3, decoder_2_out_4,
       decoder_2_out_5, DREGA, DREGACC, DREGB, DREGC, DREGD, DREGE, or_2_out, or_3_out, or_4_out, or_5_out,
       or_6_out, or_7_out;
  wire [7:0] demultiplexer_1_out_0, demultiplexer_1_out_1, demultiplexer_1_out_2, demultiplexer_1_out_3,
       demultiplexer_1_out_4, demultiplexer_1_out_5, multiplexer_1_out, notconnected_1_out;

  Decoder #(.Selector_Bits(3)) decoder_1 (
    .sel(DREG), .out_0(decoder_1_out_0), .out_1(decoder_1_out_1), .out_2(decoder_1_out_2),
    .out_3(decoder_1_out_3), .out_4(decoder_1_out_4), .out_5(decoder_1_out_5));  // open: out_6, out_7
  Decoder #(.Selector_Bits(3)) decoder_2 (
    .sel(SREG), .out_0(decoder_2_out_0), .out_1(decoder_2_out_1), .out_2(decoder_2_out_2),
    .out_3(decoder_2_out_3), .out_4(decoder_2_out_4), .out_5(decoder_2_out_5));  // open: out_6, out_7
  Demultiplexer #(.Selector_Bits(3), .Bits(8)) demultiplexer_1 (
    .sel(DREG), .in(multiplexer_1_out), .out_0(demultiplexer_1_out_0), .out_1(demultiplexer_1_out_1),
    .out_2(demultiplexer_1_out_2), .out_3(demultiplexer_1_out_3), .out_4(demultiplexer_1_out_4),
    .out_5(demultiplexer_1_out_5));  // open: out_6, out_7
  or or_1 (CNT, COUNT[0], COUNT[1], COUNT[2]);
  or or_2 (or_2_out, decoder_1_out_0, decoder_2_out_0);
  or or_3 (or_3_out, decoder_1_out_1, decoder_2_out_1);
  or or_4 (or_4_out, decoder_1_out_2, decoder_2_out_2);
  or or_5 (or_5_out, decoder_1_out_3, decoder_2_out_3);
  or or_6 (or_6_out, decoder_1_out_4, decoder_2_out_4);
  or or_7 (or_7_out, decoder_1_out_5, decoder_2_out_5);
  Register #(.Bits(8)) register_1 (.D(demultiplexer_1_out_0), .C(CLK), .en(DREGA), .Q(REGA));
  Register #(.Bits(8)) register_2 (.D(demultiplexer_1_out_1), .C(CLK), .en(DREGB), .Q(REGB));
  Register #(.Bits(8)) register_3 (.D(demultiplexer_1_out_2), .C(CLK), .en(DREGC), .Q(REGC));
  Register #(.Bits(8)) register_4 (.D(demultiplexer_1_out_3), .C(CLK), .en(DREGD), .Q(REGD));
  Register #(.Bits(8)) register_5 (.D(demultiplexer_1_out_4), .C(CLK), .en(DREGE), .Q(REGE));
  Register #(.Bits(8)) register_6 (.D(demultiplexer_1_out_5), .C(CLK), .en(DREGACC), .Q(REGACC));
  and and_1 (DREGA, or_2_out, CNT);
  and and_2 (DREGB, or_3_out, CNT);
  and and_3 (DREGC, or_4_out, CNT);
  and and_4 (DREGD, or_5_out, CNT);
  and and_5 (DREGE, or_6_out, CNT);
  and and_6 (DREGACC, or_7_out, CNT);
  Multiplexer #(.Selector_Bits(3), .Bits(8)) multiplexer_1 (
    .sel(SREG), .in_0(REGA), .in_1(REGB), .in_2(REGC), .in_3(REGD), .in_4(REGE), .in_5(REGACC),
    .in_6(notconnected_1_out), .in_7(VALUE), .out(multiplexer_1_out));
  // NotConnected on notconnected_1_out
  Multiplexer #(.Selector_Bits(3), .Bits(8)) multiplexer_2 (
    .sel(RREG), .in_0(REGA), .in_1(REGB), .in_2(REGC), .in_3(REGD), .in_4(REGE), .in_5(REGACC),
    .in_6({8{1'b0}}), .in_7({8{1'b0}}), .out(READ_REG));
endmodule
