// Digital circuit main.dig as structural Verilog
module main (
  input  clk,
  output [7:0] PC,
  output [7:0] REGA,
  output [7:0] REGB,
  output [7:0] REGC,
  output [7:0] REGD,
  output [7:0] out_7,
  output [7:0] out_8,
  output [7:0] ACC,
  output [7:0] FLAG,
  output [7:0] REGE
);

  wire A_0, A_1, A_2, A_3, A_4, A_5, A_6, A_7, and_1_out, B_0, B_1, B_2, B_3, B_4, B_5, B_6, B_7,
       button_1_out, C_0, C_1, C_2, C_3, C_4, C_5, C_6, C_7, CLOCKED_out, D_0, D_1, D_2, D_3, D_4, D_5, D_6,
       D_7, execute_1_hlt, execute_1_jmp_cond, MEM_IN, MEM_OUT, multiplexer_1_out, not_1_out, or_1_out;
  wire [2:0] decode_1_numop, execute_1_count, execute_1_dreg, execute_1_rreg, execute_1_sreg;
  wire [4:0] decode_1_ins;
  wire [7:0] DATA_MEMORY_d, demultiplexer_1_out_0, demultiplexer_1_out_1, demultiplexer_2_out_0,
       demultiplexer_2_out_1, execute_1_jmp, rom_1_d, Value;

  DipSwitch CLOCKED (.out(CLOCKED_out));
  Button button_1 (.out(button_1_out));
  Multiplexer multiplexer_1 (.sel(CLOCKED_out), .in_0(button_1_out), .in_1(clk), .out(multiplexer_1_out));
  and and_1 (and_1_out, multiplexer_1_out, not_1_out);
  Fetch fetch_1 (.CLK(and_1_out), .JMP(execute_1_jmp), .JMP_COND(execute_1_jmp_cond), .Addr(PC));
  not not_1 (not_1_out, execute_1_hlt);
  ROM #(.AddrBits(8), .isProgramMemory("true"), .Bits(8)) rom_1 (.A(PC), .sel(1'b1), .D(rom_1_d));
  Demultiplexer #(.Selector_Bits(3), .Bits(8)) demultiplexer_1 (
    .sel(execute_1_count), .in(rom_1_d), .out_0(demultiplexer_1_out_0), .out_1(demultiplexer_1_out_1));  // open: out_2, out_3, out_4, out_5, out_6, out_7
  Decode decode_1 (.IRC(demultiplexer_1_out_0), .NUMOP(decode_1_numop), .INS(decode_1_ins));
  Execute execute_1 (
    .REG_IN(out_8), .NUMOP(decode_1_numop), .INS(decode_1_ins), .OP_1(demultiplexer_1_out_1),
    .CLK(and_1_out), .MEM_IN(MEM_IN), .MEM_OUT(MEM_OUT), .COUNT(execute_1_count), .DREG(execute_1_dreg),
    .VALUE(Value), .SREG(execute_1_sreg), .RREG(execute_1_rreg), .HLT(execute_1_hlt), .JMP(execute_1_jmp),
    .JMP_COND(execute_1_jmp_cond), .Flag(FLAG));
  or or_1 (or_1_out, MEM_OUT, MEM_IN);
  Demultiplexer #(.Bits(8)) demultiplexer_2 (
    .sel(or_1_out), .in(Value), .out_0(demultiplexer_2_out_0), .out_1(demultiplexer_2_out_1));
  RegFile regfile_1 (
    .COUNT(execute_1_count), .DREG(execute_1_dreg), .VALUE(out_7), .SREG(execute_1_sreg),
    .RREG(execute_1_rreg), .CLK(and_1_out), .READ_REG(out_8), .REGACC(ACC), .REGA(REGA), .REGB(REGB),
    .REGC(REGC), .REGD(REGD), .REGE(REGE));
  EEPROMDualPort #(.AddrBits(8), .Bits(8)) DATA_MEMORY (
    .A(demultiplexer_2_out_1), .Din(ACC), .str(MEM_IN), .C(and_1_out), .ld(MEM_OUT), .D(DATA_MEMORY_d));
  Multiplexer #(.Bits(8)) multiplexer_2 (
    .sel(MEM_OUT), .in_0(demultiplexer_2_out_0), .in_1(DATA_MEMORY_d), .out(out_7));
  Seven_Seg seven_seg_1 (.a(A_7), .b(A_6), .c(A_5), .d(A_4), .e(A_3), .f(A_2), .g(A_1), .dp(A_0));
  Seven_Seg seven_seg_2 (.a(B_7), .b(B_6), .c(B_5), .d(B_4), .e(B_3), .f(B_2), .g(B_1), .dp(B_0));
  LedDriver leddriver_1 (
    .A(REGA), .B(REGB), .C(REGC), .D(REGD), .E(REGE[0]), .O_A({A_7, A_6, A_5, A_4, A_3, A_2, A_1, A_0}),
    .O_B({B_7, B_6, B_5, B_4, B_3, B_2, B_1, B_0}), .O_C({C_7, C_6, C_5, C_4, C_3, C_2, C_1, C_0}),
    .O_D({D_7, D_6, D_5, D_4, D_3, D_2, D_1, D_0}));
  Seven_Seg seven_seg_3 (.a(C_7), .b(C_6), .c(C_5), .d(C_4), .e(C_3), .f(C_2), .g(C_1), .dp(C_0));
  Seven_Seg seven_seg_4 (.a(D_7), .b(D_6), .c(D_5), .d(D_4), .e(D_3), .f(D_2), .g(D_1), .dp(D_0));

  // Other names for the same wires on the sheet: Value_R[7:0] = out_7

  // Notes on the sheet:
  //   clk: Hz: 10
  //   contents of rom_1 (hex, n*v repeats v):
  //   4*0,11,a,21,3
  //   Flag Register
  //   7. -
  //   6. -
  //   5. -
  //   4. -
  //   3. -
  //   2. -
  //   1. Zero result
  //   0. Overflow
  //   contents of DATA_MEMORY (hex, n*v repeats v):
  //   fc,60,da,f2,66,b6,be,e0,fe,f6,5,69*0,5
endmodule
